# Fritzing sketch MIDI_IN+LCD (saved by Fritzing 0.9.3b)
breadboards: 1

parts:
  U1 = mystery part, 8 pins [chip_label=TLP552]
  R1 = Resistor [tolerance=±5% resistance=220 package=THT]
  U2 = MIDI_CONN_FEMALE [package=din_5_female]
  R2 = Resistor [tolerance=±5% resistance=220 package=THT]
  C1 = Ceramic Capacitor [capacitance=100nF package="100 mil [THT, multilayer]"]
  D1 = Rectifier Diode [part_number=1N4001 package="300 mil [THT]"]
  C2 = Electrolytic Capacitor [capacitance=1µF package="100 mil [THT, electrolytic]"]
  パーツ1 = Arduino Uno (Rev3)
  LCD1 = LCD screen
  R3 = Resistor [tolerance=±5% resistance=220 package=THT]
  R4 = TRIMPOT [package=trimpot_pth_s3_lock]

nets:
  N1: U1.pin2, R1.Pin_1, D1.cathode
  N2: U1.pin3, U2.MIDI_OUT, D1.anode
  GND: U1.pin5, C1.0, C2.-, パーツ1.GND, LCD1.VSS, LCD1.R/W, LCD1.LED-, R4.CCW
  N3: U1.pin6, R2.Pin_1, パーツ1.D0/RX
  5V: U1.pin7, U1.pin8, R2.Pin_0, C1.1, C2.+, パーツ1.5V, LCD1.VDD, R3.Pin_0, R4.CW
  N4: R1.Pin_0, U2.MIDI_IN
  N5: パーツ1.D11_PWM/MOSI, LCD1.E
  N6: パーツ1.D12/MISO, LCD1.RS
  N7: パーツ1.D2, LCD1.DB7
  N8: パーツ1.D3_PWM, LCD1.DB6
  N9: パーツ1.D4, LCD1.DB5
  N10: パーツ1.D5_PWM, LCD1.DB4
  N11: LCD1.V0, R4.WIPER
  N12: LCD1.LED+, R3.Pin_1

notes:
  TLP552
  1 NC 8 VCC
  2 IN-A 7 Enable
  3 IN-K 6 VOUT
  4 NC 5 GND
  GND
  +5V
  MIDI IN
  D0
  MIDI IN
  D1
  MIDI OUT
