# Fritzing sketch SimpleSynth (saved by Fritzing 0.9.3b)
breadboards: 1

parts:
  U1 = mystery part, 8 pins [chip_label=TLP552]
  R1 = Resistor [tolerance=±5% resistance=220 package=THT]
  U2 = MIDI_CONN_FEMALE [package=din_5_female]
  R2 = Resistor [tolerance=±5% resistance=220 package=THT]
  C1 = Ceramic Capacitor [capacitance=100nF package="100 mil [THT, multilayer]"]
  D1 = Rectifier Diode [part_number=1N4001 package="300 mil [THT]"]
  C2 = Electrolytic Capacitor [capacitance=1µF package="100 mil [THT, electrolytic]"]
  パーツ1 = Arduino Uno (Rev3)
  SPKR1 = Loudspeaker

nets:
  N1: U1.pin2, R1.Pin_1, D1.cathode
  N2: U1.pin3, U2.MIDI_OUT, D1.anode
  N3: U1.pin5, C1.0, C2.-, パーツ1.GND, SPKR1.pin1
  N4: U1.pin6, R2.Pin_1, パーツ1.D0/RX
  N5: U1.pin7, U1.pin8, R2.Pin_0, C1.1, C2.+
  N6: R1.Pin_0, U2.MIDI_IN
  N7: パーツ1.D10_PWM/SS, SPKR1.pin2

notes:
  TLP552
  1 NC 8 VCC
  2 IN-A 7 Enable
  3 IN-K 6 VOUT
  4 NC 5 GND
  GND
  +5V
  MIDI IN
